// Logisim project 01_lib.circ as structural Verilog: 15 circuits, main circuit 01_Not
module _01_Not (
  input  in,
  input  in_2,
  output out,
  output out_4
);

  not not_1 (out_4, in_2);
  nand nand_1 (out, in, in);

  // Notes on the sheet:
  //   Not
endmodule

module _02_And (
  input  a,
  input  b,
  input  in_3,
  input  in_4,
  output out,
  output out_6
);

  wire nand_1_out;

  nand nand_1 (nand_1_out, a, b);
  and and_1 (out_6, in_3, in_4);
  not not_1 (out, nand_1_out);

  // Notes on the sheet:
  //   And
endmodule

module _03_Or (
  input  a,
  input  b,
  input  in_3,
  input  in_4,
  output out,
  output out_6
);

  wire nand_1_out, nand_2_out;

  nand nand_1 (nand_1_out, a, a);
  nand nand_2 (nand_2_out, b, b);
  or or_1 (out_6, in_3, in_4);
  nand nand_3 (out, nand_1_out, nand_2_out);

  // Notes on the sheet:
  //   Or
endmodule

module _04_Xor (
  input  a,
  input  b,
  input  in_3,
  input  in_4,
  output out,
  output out_6
);

  wire nand_1_out, or_1_out;

  or or_1 (or_1_out, a, b);
  nand nand_1 (nand_1_out, a, b);
  xor xor_1 (out_6, in_3, in_4);
  and and_1 (out, or_1_out, nand_1_out);

  // Notes on the sheet:
  //   Xor
endmodule

module _05_Mux (
  input  a,
  input  sel,
  input  b,
  input  in_4,
  input  in_5,
  input  in_6,
  output out_7,
  output out_8
);

  wire and_1_out, and_2_out, not_1_out;

  not not_1 (not_1_out, sel);
  and and_1 (and_1_out, a, sel);
  and and_2 (and_2_out, b, not_1_out);
  Multiplexer #(.enable("false")) multiplexer_1 (.in0(in_4), .in1(in_5), .out(out_8), .sel(in_6));
  or or_1 (out_7, and_1_out, and_2_out);

  // Notes on the sheet:
  //   Mux
endmodule

module _06_Dmux (
  input  in_1,
  input  sel,
  input  in_3,
  input  in_4,
  output a,
  output b,
  output out_7,
  output out_8
);

  wire not_1_out;

  Demultiplexer #(.enable("false")) demultiplexer_1 (.out0(out_7), .out1(out_8), .in(in_3), .sel(in_4));
  not not_1 (not_1_out, sel);
  and and_1 (a, in_1, not_1_out);
  and and_2 (b, in_1, sel);

  // Notes on the sheet:
  //   DMux
endmodule

module _07_Not16 (
  input  in_1,
  input  in_2,
  input  in_3,
  input  in_4,
  input  in_5,
  input  in_6,
  input  in_7,
  input  in_8,
  input  in_9,
  input  in_10,
  input  in_11,
  input  in_12,
  input  in_13,
  input  in_14,
  input  in_15,
  input  in_16,
  input  [15:0] in_17,
  output out_18,
  output out_19,
  output out_20,
  output out_21,
  output out_22,
  output out_23,
  output out_24,
  output out_25,
  output out_26,
  output out_27,
  output out_28,
  output out_29,
  output out_30,
  output out_31,
  output out_32,
  output out_33,
  output [15:0] out_34
);

  not not_1 (out_18, in_1);
  not not_2 (out_19, in_2);
  not not_3 (out_20, in_3);
  not not_4 (out_21, in_4);
  not not_5 (out_23, in_6);
  not not_6 (out_24, in_7);
  not not_7 (out_22, in_5);
  assign out_34 = ~in_17;  // NOT_Gate not_8, 16 bits wide
  not not_9 (out_26, in_9);
  not not_10 (out_25, in_8);
  not not_11 (out_29, in_12);
  not not_12 (out_28, in_11);
  not not_13 (out_27, in_10);
  not not_14 (out_30, in_13);
  not not_15 (out_31, in_14);
  not not_16 (out_32, in_15);
  not not_17 (out_33, in_16);

  // Notes on the sheet:
  //   Not16
endmodule

module _08_And16 (
  input  in_1,
  input  in_2,
  input  in_3,
  input  in_4,
  input  in_5,
  input  in_6,
  input  [15:0] in_7,
  input  in_8,
  input  in_9,
  input  [15:0] in_10,
  input  in_11,
  input  in_12,
  input  in_13,
  input  in_14,
  input  in_15,
  input  in_16,
  input  in_17,
  input  in_18,
  input  in_19,
  input  in_20,
  input  in_21,
  input  in_22,
  input  in_23,
  input  in_24,
  input  in_25,
  input  in_26,
  input  in_27,
  input  in_28,
  input  in_29,
  input  in_30,
  input  in_31,
  input  in_32,
  input  in_33,
  input  in_34,
  output out_35,
  output out_36,
  output out_37,
  output out_38,
  output [15:0] out_39,
  output out_40,
  output out_41,
  output out_42,
  output out_43,
  output out_44,
  output out_45,
  output out_46,
  output out_47,
  output out_48,
  output out_49,
  output out_50,
  output out_51
);

  and and_1 (out_35, in_1, in_2);
  and and_2 (out_36, in_3, in_4);
  and and_3 (out_37, in_5, in_6);
  and and_4 (out_38, in_8, in_9);
  and and_5 (out_40, in_11, in_12);
  and and_6 (out_41, in_13, in_14);
  and and_7 (out_42, in_15, in_16);
  and and_8 (out_43, in_17, in_18);
  and and_9 (out_44, in_19, in_20);
  and and_10 (out_45, in_21, in_22);
  and and_11 (out_46, in_23, in_24);
  and and_12 (out_47, in_25, in_26);
  and and_13 (out_48, in_27, in_28);
  and and_14 (out_49, in_29, in_30);
  and and_15 (out_50, in_31, in_32);
  and and_16 (out_51, in_33, in_34);
  assign out_39 = in_7 & in_10;  // AND_Gate and_17, 16 bits wide

  // Notes on the sheet:
  //   And16
endmodule

module _09_Or16 (
  input  in_1,
  input  in_2,
  input  in_3,
  input  in_4,
  input  [15:0] in_5,
  input  in_6,
  input  in_7,
  input  [15:0] in_8,
  input  in_9,
  input  in_10,
  input  in_11,
  input  in_12,
  input  in_13,
  input  in_14,
  input  in_15,
  input  in_16,
  input  in_17,
  input  in_18,
  input  in_19,
  input  in_20,
  input  in_21,
  input  in_22,
  input  in_23,
  input  in_24,
  input  in_25,
  input  in_26,
  input  in_27,
  input  in_28,
  input  in_29,
  input  in_30,
  input  in_31,
  input  in_32,
  input  in_33,
  input  in_34,
  output out_35,
  output out_36,
  output [15:0] out_37,
  output out_38,
  output out_39,
  output out_40,
  output out_41,
  output out_42,
  output out_43,
  output out_44,
  output out_45,
  output out_46,
  output out_47,
  output out_48,
  output out_49,
  output out_50,
  output out_51
);

  or or_1 (out_35, in_1, in_2);
  or or_2 (out_36, in_3, in_4);
  or or_3 (out_38, in_6, in_7);
  or or_4 (out_39, in_9, in_10);
  or or_5 (out_40, in_11, in_12);
  or or_6 (out_41, in_13, in_14);
  or or_7 (out_42, in_15, in_16);
  or or_8 (out_43, in_17, in_18);
  or or_9 (out_44, in_19, in_20);
  or or_10 (out_45, in_21, in_22);
  or or_11 (out_46, in_23, in_24);
  or or_12 (out_47, in_25, in_26);
  or or_13 (out_48, in_27, in_28);
  or or_14 (out_49, in_29, in_30);
  or or_15 (out_50, in_31, in_32);
  or or_16 (out_51, in_33, in_34);
  assign out_37 = in_5 | in_8;  // OR_Gate or_17, 16 bits wide

  // Notes on the sheet:
  //   Or16
endmodule

module _10_Mux16 (
  input  in_1,
  input  in_2,
  input  in_3,
  input  in_4,
  input  in_5,
  input  in_6,
  input  in_7,
  input  in_8,
  input  in_9,
  input  in_10,
  input  in_11,
  input  in_12,
  input  in_13,
  input  in_14,
  input  in_15,
  input  in_16,
  input  in_17,
  input  in_18,
  input  in_19,
  input  in_20,
  input  in_21,
  input  in_22,
  input  in_23,
  input  in_24,
  input  in_25,
  input  in_26,
  input  in_27,
  input  in_28,
  input  in_29,
  input  in_30,
  input  in_31,
  input  in_32,
  input  sel,
  input  [15:0] in_34,
  input  [15:0] in_35,
  input  in_36,
  output out_37,
  output out_38,
  output out_39,
  output out_40,
  output out_41,
  output out_42,
  output out_43,
  output out_44,
  output out_45,
  output out_46,
  output out_47,
  output out_48,
  output out_49,
  output out_50,
  output out_51,
  output out_52,
  output [15:0] out_53
);

  Multiplexer #(.enable("false")) multiplexer_1 (.in0(in_1), .in1(in_17), .out(out_37), .sel(sel));
  Multiplexer #(.enable("false")) multiplexer_2 (.in0(in_2), .in1(in_18), .out(out_38), .sel(sel));
  Multiplexer #(.enable("false")) multiplexer_3 (.in0(in_3), .in1(in_19), .out(out_39), .sel(sel));
  Multiplexer #(.width(16), .enable("false")) multiplexer_4 (.in0(in_34), .in1(in_35), .out(out_53), .sel(in_36));
  Multiplexer #(.enable("false")) multiplexer_5 (.in0(in_4), .in1(in_20), .out(out_40), .sel(sel));
  Multiplexer #(.enable("false")) multiplexer_6 (.in0(in_5), .in1(in_21), .out(out_41), .sel(sel));
  Multiplexer #(.enable("false")) multiplexer_7 (.in0(in_6), .in1(in_22), .out(out_42), .sel(sel));
  Multiplexer #(.enable("false")) multiplexer_8 (.in0(in_7), .in1(in_23), .out(out_43), .sel(sel));
  Multiplexer #(.enable("false")) multiplexer_9 (.in0(in_8), .in1(in_24), .out(out_44), .sel(sel));
  Multiplexer #(.enable("false")) multiplexer_10 (.in0(in_9), .in1(in_25), .out(out_45), .sel(sel));
  Multiplexer #(.enable("false")) multiplexer_11 (.in0(in_10), .in1(in_26), .out(out_46), .sel(sel));
  Multiplexer #(.enable("false")) multiplexer_12 (.in0(in_11), .in1(in_27), .out(out_47), .sel(sel));
  Multiplexer #(.enable("false")) multiplexer_13 (.in0(in_12), .in1(in_28), .out(out_48), .sel(sel));
  Multiplexer #(.enable("false")) multiplexer_14 (.in0(in_13), .in1(in_29), .out(out_49), .sel(sel));
  Multiplexer #(.enable("false")) multiplexer_15 (.in0(in_14), .in1(in_30), .out(out_50), .sel(sel));
  Multiplexer #(.enable("false")) multiplexer_16 (.in0(in_15), .in1(in_31), .out(out_51), .sel(sel));
  Multiplexer #(.enable("false")) multiplexer_17 (.in0(in_16), .in1(in_32), .out(out_52), .sel(sel));

  // Notes on the sheet:
  //   Mux16
endmodule

module _11_Or8Way (
  input  in_1,
  input  in_2,
  input  in_3,
  input  in_4,
  input  in_5,
  input  in_6,
  input  in_7,
  input  in_8,
  input  in_9,
  input  in_10,
  input  in_11,
  input  in_12,
  input  in_13,
  input  in_14,
  input  in_15,
  input  in_16,
  output out_17,
  output out_18
);

  wire or_1_out, or_3_out, or_4_out, or_5_out, or_6_out, or_7_out;

  or or_1 (or_1_out, in_1, in_2);
  or or_2 (out_18, in_9, in_10, in_11, in_12, in_13, in_14, in_15, in_16);
  or or_3 (or_3_out, or_1_out, in_3);
  or or_4 (or_4_out, or_3_out, in_4);
  or or_5 (or_5_out, or_4_out, in_5);
  or or_6 (or_6_out, or_5_out, in_6);
  or or_7 (or_7_out, or_6_out, in_7);
  or or_8 (out_17, or_7_out, in_8);

  // Notes on the sheet:
  //   Or8Way
endmodule

module _12_Mux4Way16 (
  input  [15:0] a,
  input  [15:0] b,
  input  [15:0] c,
  input  [15:0] d,
  input  sel_0,
  input  sel_1,
  output [15:0] out_7,
  output ands,
  output ors
);

  wire [15:0] multiplexer_1_out, multiplexer_2_out;

  Multiplexer #(.width(16), .enable("false")) multiplexer_1 (.in0(a), .in1(b), .out(multiplexer_1_out), .sel(ors));
  Multiplexer #(.width(16), .enable("false")) multiplexer_2 (.in0(c), .in1(d), .out(multiplexer_2_out), .sel(ands));
  and and_1 (ands, sel_0, sel_1);
  or or_1 (ors, sel_0, sel_1);
  Multiplexer #(.width(16), .enable("false")) multiplexer_3 (
    .in0(multiplexer_1_out), .in1(multiplexer_2_out), .out(out_7), .sel(sel_1));

  // Notes on the sheet:
  //   Mux4Way16
  //   cdmux
  //   abmux
endmodule

module _13_Mux8Way16 (
  input  [15:0] in_1,
  input  [15:0] in_2,
  input  [15:0] in_3,
  input  [15:0] in_4,
  input  [15:0] in_5,
  input  [15:0] in_6,
  input  in_7,
  input  in_8,
  input  in_9,
  input  [15:0] in_10,
  input  [15:0] in_11,
  input  [15:0] in_12,
  input  [15:0] in_13,
  input  [15:0] in_14,
  input  [15:0] in_15,
  input  [15:0] in_16,
  input  [15:0] in_17,
  input  [2:0] in_18,
  output [15:0] out_19,
  output [15:0] out_20
);

  wire [15:0] multiplexer_1_out, multiplexer_2_out, multiplexer_3_out, multiplexer_5_out;

  Multiplexer #(.width(16), .enable("false")) multiplexer_1 (
    .in0(in_1), .in1(in_2), .out(multiplexer_1_out), .sel(in_7));
  Multiplexer #(.width(16), .enable("false")) multiplexer_2 (
    .in0(in_3), .in1(in_4), .out(multiplexer_2_out), .sel(in_7));
  Multiplexer #(.width(16), .enable("false")) multiplexer_3 (
    .in0(in_5), .in1(in_6), .out(multiplexer_3_out), .sel(in_7));
  Multiplexer #(.select(3), .width(16), .enable("false")) multiplexer_4 (
    .in0(in_10), .in1(in_11), .in2(in_12), .in3(in_13), .in4(in_14), .in5(in_15), .in6(in_16), .in7(in_17),
    .out(out_20), .sel(in_18));
  Multiplexer #(.width(16), .enable("false")) multiplexer_5 (
    .in0(multiplexer_1_out), .in1(multiplexer_2_out), .out(multiplexer_5_out), .sel(in_8));
  Multiplexer #(.width(16), .enable("false")) multiplexer_6 (
    .in0(multiplexer_5_out), .in1(multiplexer_3_out), .out(out_19), .sel(in_9));

  // Notes on the sheet:
  //   Mux8Way16
endmodule

module _14_DMux4Way (
  input  in_1,
  input  in_2,
  input  in_3,
  output out_4,
  output out_5,
  output out_6,
  output out_7
);

  wire demultiplexer_1_out0, demultiplexer_1_out1;

  Demultiplexer #(.enable("false")) demultiplexer_1 (
    .out0(demultiplexer_1_out0), .out1(demultiplexer_1_out1), .in(in_1), .sel(in_2));
  Demultiplexer #(.enable("false")) demultiplexer_2 (.out0(out_4), .out1(out_5), .in(demultiplexer_1_out0), .sel(in_3));
  Demultiplexer #(.enable("false")) demultiplexer_3 (.out0(out_6), .out1(out_7), .in(demultiplexer_1_out1), .sel(in_3));
endmodule

module _15_DMux8Way (
  input  in_1,
  input  in_2,
  input  in_3,
  input  in_4
);

  wire demultiplexer_1_out0, demultiplexer_1_out1, demultiplexer_2_out0, demultiplexer_2_out1,
       demultiplexer_3_out0, demultiplexer_3_out1;

  Demultiplexer #(.enable("false")) demultiplexer_1 (
    .out0(demultiplexer_1_out0), .out1(demultiplexer_1_out1), .in(in_1), .sel(in_2));
  Demultiplexer #(.enable("false")) demultiplexer_2 (
    .out0(demultiplexer_2_out0), .out1(demultiplexer_2_out1), .in(demultiplexer_1_out0), .sel(in_3));
  Demultiplexer #(.enable("false")) demultiplexer_3 (
    .out0(demultiplexer_3_out0), .out1(demultiplexer_3_out1), .in(demultiplexer_1_out1), .sel(in_3));
  Demultiplexer #(.enable("false")) demultiplexer_4 (.in(demultiplexer_2_out0), .sel(in_4));  // open: out0, out1
  Demultiplexer #(.enable("false")) demultiplexer_5 (.in(demultiplexer_2_out1), .sel(in_4));  // open: out0, out1
  Demultiplexer #(.enable("false")) demultiplexer_6 (.in(demultiplexer_3_out0), .sel(in_4));  // open: out0, out1
  Demultiplexer #(.enable("false")) demultiplexer_7 (.in(demultiplexer_3_out1), .sel(in_4));  // open: out0, out1
endmodule
