// Logisim project 02_lib.circ as structural Verilog: 1 circuit, main circuit main
module main (
  input  [15:0] x,
  input  [15:0] y,
  input  [15:0] in_3,
  input  \zx__X输入置0 ,
  input  \zy__Y输入置零 ,
  input  \nx__x输入取反 ,
  input  \ny__y输入取反 ,
  input  \f__功能码1代表Add__0代表And ,
  input  \no_输入取反 ,
  output [15:0] fx,
  output [15:0] fy,
  output [15:0] out
);

  wire [15:0] adder_1_out, and_1_out, multiplexer_1_out, multiplexer_3_out, multiplexer_5_out, not_1_out,
       not_2_out, not_3_out;

  Multiplexer #(.width(16), .enable("false")) multiplexer_1 (
    .in0(in_3), .in1(x), .out(multiplexer_1_out), .sel(\zx__X输入置0 ));
  assign not_1_out = ~multiplexer_1_out;  // NOT_Gate not_1, 16 bits wide
  Multiplexer #(.width(16), .enable("false")) multiplexer_2 (
    .in0(multiplexer_1_out), .in1(not_1_out), .out(fx), .sel(\nx__x输入取反 ));
  Multiplexer #(.width(16), .enable("false")) multiplexer_3 (
    .in0(in_3), .in1(y), .out(multiplexer_3_out), .sel(\zy__Y输入置零 ));
  Adder #(.width(16)) adder_1 (.a(fy), .b(fx), .out(adder_1_out));  // open: cin, cout
  assign not_2_out = ~multiplexer_3_out;  // NOT_Gate not_2, 16 bits wide
  Multiplexer #(.width(16), .enable("false")) multiplexer_4 (
    .in0(multiplexer_3_out), .in1(not_2_out), .out(fy), .sel(\ny__y输入取反 ));
  assign and_1_out = fy & fx;  // AND_Gate and_1, 16 bits wide
  Multiplexer #(.width(16), .enable("false")) multiplexer_5 (
    .in0(adder_1_out), .in1(and_1_out), .out(multiplexer_5_out), .sel(\f__功能码1代表Add__0代表And ));
  assign not_3_out = ~multiplexer_5_out;  // NOT_Gate not_3, 16 bits wide
  Multiplexer #(.width(16), .enable("false")) multiplexer_6 (
    .in0(multiplexer_5_out), .in1(not_3_out), .out(out), .sel(\no_输入取反 ));
endmodule
