// Logisim project 03_lib.circ as structural Verilog: 1 circuit, main circuit main
module main (
  input  in_1,
  input  in_2,
  input  in_3,
  input  in_4,
  input  in_5,
  input  in_6,
  input  in_7,
  input  in_8,
  output out_9,
  output out_10,
  output out_11,
  output out_12,
  output out_13,
  output out_14
);

  wire clock_1_out, clock_2_out, clock_3_out, clock_4_out, multiplexer_1_out, multiplexer_2_out,
       multiplexer_3_out;

  Clock clock_1 (.out(clock_1_out));
  Multiplexer #(.enable("false")) multiplexer_1 (.in0(out_11), .in1(in_4), .out(multiplexer_1_out), .sel(in_5));
  D_Flip_Flop d_ff_1 (.clk(clock_1_out), .D(in_1), .Q(out_9), .Qn(out_10));  // open: preset, en, reset
  Clock clock_2 (.out(clock_2_out));
  Clock clock_3 (.out(clock_3_out));
  Multiplexer #(.enable("false")) multiplexer_2 (.in0(out_13), .in1(in_6), .out(multiplexer_2_out), .sel(in_8));
  Multiplexer #(.enable("false")) multiplexer_3 (.in0(out_14), .in1(in_7), .out(multiplexer_3_out), .sel(in_8));
  D_Flip_Flop d_ff_2 (.clk(clock_2_out), .D(multiplexer_1_out), .Q(out_11));  // open: Qn, preset, en, reset
  D_Flip_Flop d_ff_3 (.clk(clock_3_out), .D(multiplexer_2_out), .Q(out_13));  // open: Qn, preset, en, reset
  D_Flip_Flop d_ff_4 (.clk(clock_3_out), .D(multiplexer_3_out), .Q(out_14));  // open: Qn, preset, en, reset
  Register #(.width(1)) register_1 (.D(in_2), .en(in_3), .Q(out_12), .clk(clock_4_out));  // open: clr
  Clock clock_4 (.out(clock_4_out));
endmodule
